# Fritzing sketch PID_Rough_Draft (saved by Fritzing 0.9.3b)
breadboards: 5

parts:
  Part1 = Arduino Uno (Rev3)
  Q1 = PHOTOTRANSISTOR REFLECTIVE OBJECT SENSOR [package=qrb1114-side]
  Q2 = NPN-Transistor [package="SOT-23 [SMD]"]
  R2 = Resistor [tolerance=±5% resistance=220 package=THT]
  M2 = DC Motor
  D2 = Diode [package=diode-1n4148]
  R3 = Rotary Potentiometer (Small) [maximum_resistance=100kΩ package=THT]
  Part2 = Arduino Uno (Rev3)
  VCC3 = Battery  # not connected
  VCC5 = Battery  # not connected
  START_2 = Toggle Switch [package=THT]
  LED1 = LED - 5mm [color="Red (633nm)" package="5 mm [THT]"]  # not connected
  Adjust_Brightness_++_-- = Pushbutton [package="[THT]"]
  S3 = Pushbutton [package="[THT]"]
  10K_Resistor = Resistor [tolerance=±5% resistance=10k package=THT]
  LED2 = LED - 5mm [color="Red (633nm)" package="5 mm [THT]"]  # not connected
  SELECT_4 = Toggle Switch [package=THT]
  Q3 = NPN-Transistor [package="SOT-23 [SMD]"]  # not connected

nets:
  N1: Part1.D11_PWM/MOSI, R2.Pin_0
  N2: Part1.D2, Part1.D3_PWM, Q1.C
  N3: Part1.5V, Q1.A, Q1.K
  N4: Part1.GND, Q1.E, Q2.1
  N5: Q2.0, R2.Pin_1
  N6: M2.pin_1, D2.C
  N7: R3.leg1, Part2.D8, Part2.D2, Part2.D4, Part2.D7, Part2.5V, START_2.L1, START_2.COM, Adjust_Brightness_++_--.Pin_3, Adjust_Brightness_++_--.Pin_4, S3.Pin_3, S3.Pin_4, 10K_Resistor.Pin_0, SELECT_4.L1, SELECT_4.COM
  N8: R3.wiper, Part2.A0
  N9: R3.leg2, Part2.GND, 10K_Resistor.Pin_1
  N10: Adjust_Brightness_++_--.Pin_1, Adjust_Brightness_++_--.Pin_2
  N11: S3.Pin_1, S3.Pin_2
